# Fritzing sketch AlarmanlageV3 (saved by Fritzing 0.9.5d)

parts:
  Bauteil1 = Arduino Mega 2560 (Rev3)
  Bauteil2 = Arduino Wireless SD Shield
  Q1 = TRANSISTOR_NPN [package=to-92]
  S1 = Reed switch [package=THT]
  S2 = Reed switch [package=THT]
  S3 = Reed switch [package=THT]
  Display1 = LCD screen 16x2 IIC [part_number=101290]
  K1 = Relay [part_number=FRS1B-S package=THT]
  Power_plug1 = Power plug
  Bauteil3 = RFID-RC522-v2

nets:
  N1: Bauteil1.A0, Bauteil2.A0
  N2: Bauteil1.A1, Bauteil2.A1
  N3: Bauteil1.A2, Bauteil2.A2
  N4: Bauteil1.A3, Bauteil2.A3
  N5: Bauteil1.A4, Bauteil2.A4
  N6: Bauteil1.A5, Bauteil2.A5
  N7: Bauteil1.D21/SCL, Display1.SCL
  N8: Bauteil1.D20/SDA, Display1.SDA
  N9: Bauteil1.AREF, Bauteil2.AREF
  GND: Bauteil1.GND, Bauteil2.GND, Bauteil2.N$126, Q1.C, Display1.GND, K1.COIL1, Power_plug1.GND
  N10: Bauteil1.D13_PWM, Bauteil2.D13
  N11: Bauteil1.D12_PWM, Bauteil2.D12
  N12: Bauteil1.D11_PWM, Bauteil2.D11
  N13: Bauteil1.D10_PWM, Bauteil2.D10
  N14: Bauteil1.D9_PWM, Bauteil2.D9
  N15: Bauteil1.D8_PWM, Bauteil2.D8
  N16: Bauteil1.RESET, Bauteil2.RESET, Bauteil2.N$127, Q1.E
  3.3V: Bauteil1.3V3, Bauteil2.3.3V, Bauteil3.3.3V
  5V: Bauteil1.5V, Bauteil2.+5V, S1.pin_2, S2.pin_2, S3.pin_2, Display1.VCC
  VIN: Bauteil1.VIN, Bauteil2.VIN, Power_plug1.VCC
  N17: Bauteil1.D0_RX0, Bauteil2.ARDUINO-RX(0)
  N18: Bauteil1.D1_TX0, Bauteil2.ARDUINO-TX(1)
  N19: Bauteil1.D2_PWM, Bauteil2.D2
  N20: Bauteil1.D3_PWM, Bauteil2.D3
  N21: Bauteil1.D4_PWM, Bauteil2.SD_CS
  N22: Bauteil1.D5_PWM, Bauteil2.D5
  N23: Bauteil1.D6_PWM, Bauteil2.D6
  N24: Bauteil1.D7_PWM, Bauteil2.D7
  N25: Bauteil1.D22, K1.C1
  N26: Bauteil1.D34, S1.pin_1
  N27: Bauteil1.D36, S2.pin_1
  N28: Bauteil1.D38, S3.pin_1
  N29: Bauteil1.D53, Bauteil3.SDA
  N30: Bauteil2.N$121, Q1.B

notes:
  Tür Schalter

custom parts:
  LCD screen 16x2 IIC: LCD screen with HD44780 controller enables showing text, symbols, value or anything else that comes from Croduino/Arduino. It is capable of showing 16 symbols in two lines and therefore can be used in many projects that need to send clearly visible and legible output information.. • Color of symbols: White • Backlight: Blue • Dimensions: 80 x 36 x 12 mm • Screen dimensions: 64.5 x 16 mm •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
  RFID-RC522-v2: A simple China made RFID-RC522 Reader; do check the pin labels, as this is a MFRC522 based clone.

// code stored in the sketch: Untitled2.ino
#include "Sodaq_wdt.h"

#ifdef ARDUINO_ARCH_AVR

#define DIAG_STREAM Serial

#elif ARDUINO_ARCH_SAMD

#define DIAG_STREAM SerialUSB

#endif



#include <SPI.h>      
#include <MFRC522.h>  
#include <Wire.h> 
#include <LiquidCrystal_I2C.h>
#include <SD.h>

#define RST_PIN     5
#define SS_PIN      53 

LiquidCrystal_I2C lcd(0x27, 16, 2);
MFRC522 mfrc522(SS_PIN, RST_PIN); 

//const int chipSelect = 5;

byte Henry_uid[] = {0xA0, 0xC1, 0xF2, 0x32};
byte Barbara_uid[] = {0xF9, 0xA5, 0x36, 0xC1};
byte Andy_uid[] = {0x07, 0x49, 0x1E, 0xB5};
byte Nilse_uid[] = {0x49, 0xCC, 0x50, 0xC2};
byte Ersatz2_uid[] = {0xD0, 0x11, 0x25, 0x32};
byte Ersatz1_uid[] = {0x67, 0x37, 0x1E, 0xB5};

int Henry_check = false;
int Barbara_check = false;
int Ersatz1_check = false;
int Ersatz2_check = false;
int Nilse_check = false;
int Andy_check = false;
int Alarm_check = false;
int Zaehler = 1;
int TimerAlarm =60; //Sekunden
int Sattelkammer =38;
int Spinn =34;
int Gruen =36;
int Hupe = 490;
int b = 0;
int Relay = 22;

byte a[] = {
  B01010,
  B00000,
  B01110,
  B00001,
  B01111,
  B10001,
  B01111,
  B00000
};
int Laut = 1; //0 Aus 1 An
      void wdtrest(){
if (sodaq_wdt_flag) {
    sodaq_wdt_flag = false;
    sodaq_wdt_reset();
  Serial.println("WDT interrupt has been triggered");
  }
    }
void Alarmabak(){
  // Alarm anlage Aktiwiren/deaktiwiren
      if (Alarm_check == false){
        Alarm_check = true;
        lcd.backlight();
        lcd.setCursor(0,1);
        lcd.print("Alarm aktiviert");
      if(digitalRead(Sattelkammer)||digitalRead(Spinn)||digitalRead(Gruen)){
         sodaq_wdt_enable(WDT_PERIOD_1DIV64);
        delay(10000);
      }
      delay(10000);
      }

       else {
        Alarm_check = false;
        lcd.backlight();
        lcd.setCursor(0,1);
        lcd.print("Alarm deaktiviert");

 }

    }
    void laut(){
      Serial.println(Laut);
    while(Zaehler <= 60){
      if(Laut == 1){
 digitalWrite(Relay, LOW);
  wdtrest();
 delay(500);
   wdtrest();
    delay(500);
 digitalWrite(Relay, HIGH);
      }
      wdtrest();
  wdtrest();
 Serial.print(Zaehler);
 Serial.println(".Alarm");
     Zaehler++;
 wdtrest();
    }
    
     digitalWrite(Relay, LOW);
     Alarm_check = false;
     Serial.println("deaktivirt");
     Zaehler = 1;
     delay(10000);

    }

  void uid(){
    wdtrest();
      // put your main code here, to run repeatedly:
  if (mfrc522.PICC_IsNewCardPresent() && mfrc522.PICC_ReadCardSerial() ) {
    Serial.print("Gelesene UID:");
    for (byte i = 0; i < mfrc522.uid.size; i++) {
      // Abstand zwischen HEX-Zahlen und führende Null bei Byte < 16
      Serial.print(mfrc522.uid.uidByte[i] < 0x10 ? " 0" : " ");
      Serial.print(mfrc522.uid.uidByte[i], HEX);
      
    }
    wdtrest();
        Henry_check = true;
    for (int j=0; j<4; j++) {
      if (mfrc522.uid.uidByte[j] != Henry_uid[j]) {
        Henry_check = false;
      }
    }
    wdtrest();
 
    // UID Vergleichen mit red_uid
    Barbara_check = true;
    for (int j=0; j<4; j++) {
      if (mfrc522.uid.uidByte[j] != Barbara_uid[j]) {
        Barbara_check = false;
      }
    }
    wdtrest();
        Andy_check = true;
    for (int j=0; j<4; j++) {
      if (mfrc522.uid.uidByte[j] != Andy_uid[j]) {
        Andy_check = false;
      }
    }
    wdtrest();
         Nilse_check = true;
    for (int j=0; j<4; j++) {
      if (mfrc522.uid.uidByte[j] != Nilse_uid[j]) {
        Nilse_check = false;
      }
    }
    wdtrest();
            Ersatz1_check = true;
    for (int j=0; j<4; j++) {
      if (mfrc522.uid.uidByte[j] != Ersatz1_uid[j]) {
        Ersatz1_check = false;
      }
    }
wdtrest();
       Ersatz2_check = true;
    for (int j=0; j<4; j++) {
      if (mfrc522.uid.uidByte[j] != Ersatz2_uid[j]) {
        Ersatz2_check = false;
      }
    }
    wdtrest();
  }
  wdtrest();
  }
  void displayresat(){
    Alarmabak();
delay(2000);
wdtrest();
delay(2000);
wdtrest();
delay(2000);
wdtrest();
delay(2000);
wdtrest();
delay(2000);
wdtrest();
    lcd.noBacklight();
        lcd.clear();
  }
void setup() {
  SPI.begin();      
  mfrc522.PCD_Init();
  lcd.init();
      lcd.home();
           lcd.createChar(1, a);
      lcd.home();
          lcd.noBacklight();
        lcd.clear();
 TimerAlarm = TimerAlarm * 1000;
 pinMode(Sattelkammer, INPUT_PULLUP);
 pinMode(Spinn, INPUT_PULLUP);
 pinMode(Gruen, INPUT_PULLUP);
 TimerAlarm = millis();
 Serial.begin(9600);
 pinMode(Hupe, OUTPUT);
 pinMode(Relay, OUTPUT);
 digitalWrite(Relay, LOW);
 delay(1000);
 lcd.backlight();
  delay(1000);
  lcd.noBacklight();
 Alarm_check = true;
 if(digitalRead(Sattelkammer)||digitalRead(Spinn)||digitalRead(Gruen)){
  Alarm_check = false;
  Serial.println("deaktivirt");
  lcd.print("deaktiviert");
  lcd.backlight();
  delay(500);
  lcd.noBacklight();
  delay(500);
  lcd.backlight();
  delay(500);
  lcd.noBacklight();
  delay(500);
  lcd.backlight();
  delay(500);
  lcd.noBacklight();
  delay(500);
  lcd.backlight();
  delay(500);
  lcd.noBacklight();
  delay(500);
  lcd.backlight();
  delay(500);
  lcd.noBacklight();
  delay(500);
  lcd.backlight();
  delay(500);
  lcd.noBacklight();
  delay(500);
  lcd.noBacklight();
  lcd.clear();
 }
 Serial.println("Start up");
 sodaq_wdt_enable(WDT_PERIOD_4X);
}
void loop() {
    wdtrest();
    uid();
 

    if (Henry_check) {
         lcd.setCursor(0,0);
        lcd.print("Hallo Henry");
displayresat();
    }
 
    if (Barbara_check) {
        lcd.setCursor(0,0);
        lcd.print("Hallo B");
        lcd.setCursor(7,0);
        lcd.write(byte(1));
        lcd.setCursor(8,0);
        lcd.print("rbel");
displayresat();
    }
 if (Andy_check) {
        lcd.setCursor(0,0);
        lcd.print("Hallo Andy");
displayresat();
    }
     if (Ersatz1_check) {
        lcd.setCursor(0,0);
        lcd.print("Hallo Ersatz1");
displayresat();
    }
     if (Ersatz2_check) {
        lcd.setCursor(0,0);
        lcd.print("Hallo Ersatz2");
displayresat();
    }
         if (Nilse_check) {
        lcd.setCursor(0,0);
        lcd.print("Hallo Herr Niehls");
displayresat();
    }

    // Versetzt die gelesene Karte in einen Ruhemodus, um nach anderen Karten suchen zu können.


  
 if(digitalRead(Sattelkammer)&&Alarm_check == true){
 Serial.println("Alarm");
laut();
 }
  if(digitalRead(Spinn)&&Alarm_check == true){
Serial.println("Alarm");
laut();
 }
  if(digitalRead(Gruen)&&Alarm_check == true){
Serial.println("Alarm");
laut();
 }}
