# Fritzing sketch Arlarm Haupt (saved by Fritzing 0.9.4)
breadboards: 1

parts:
  Bauteil1 = Arduino Mega 2560 (Rev3)
  Bauteil2 = NRF24L01+ Breakout Board  # not connected
  LED1 = RGB LED - (4 legs) [package="5 mm [THT]"]
  Laser = LED - 5mm [color="Red (633nm)" package="5 mm [THT]"]
  Laser_2 = LED - 5mm [color="Red (633nm)" package="5 mm [THT]"]
  R1 = Photocell (LDR) [package=THT]
  R2 = Photocell (LDR) [package=THT]
  R3 = Resistor [tolerance=±5% resistance=220 package=THT]
  R4 = Resistor [tolerance=±5% resistance=220 package=THT]
  LCD1 = LCD screen  # not connected

nets:
  N1: Bauteil1.A0, R2.pin_0, R3.Pin_1
  N2: Bauteil1.A1, R1.pin_1, R4.Pin_0
  N3: Bauteil1.GND, LED1.blue_cathode, Laser.anode, Laser_2.anode, R3.Pin_0, R4.Pin_1
  N4: Bauteil1.D10_PWM, LED1.red_cathode
  N5: Bauteil1.D9_PWM, LED1.common_anode
  N6: Bauteil1.D8_PWM, LED1.green_cathode
  N7: Bauteil1.5V, R1.pin_0, R2.pin_1
  N8: Bauteil1.D2_PWM, Laser_2.cathode
  N9: Bauteil1.D3_PWM, Laser.cathode
